# Fritzing sketch wiring_schema (saved by Fritzing 0.9.2b)
breadboards: 1

parts:
  Parte1 = Arduino Uno (Rev3)
  LCD1 = LCD screen
  LED1 = LED - 5mm [color="Red (633nm)" package="5 mm [THT]"]
  LED3 = LED - 5mm [color="Red (633nm)" package="5 mm [THT]"]
  LED4 = LED - 5mm [color="Yellow (595nm)" package="5 mm [THT]"]
  LED5 = LED - 5mm [color="Yellow (595nm)" package="5 mm [THT]"]
  R1 = Resistor [tolerance=±5% resistance=270 package=THT]
  R2 = Resistor [tolerance=±5% resistance=270 package=THT]
  R3 = Resistor [tolerance=±5% resistance=270 package=THT]
  Parte2 = Triple Axis Accelerometer Breakout - ADXL335
  R4 = Temperature Sensor (Thermistor) [thermistor_type=NTC package=THT]
  R5 = Resistor [tolerance=±5% resistance=10k package=THT]
  R6 = Resistor [tolerance=±5% resistance=270 package=THT]
  RE1 = Rotary Encoder [package=THT]

nets:
  N1: Parte1.A0, Parte2.XOUT
  N2: Parte1.A1, Parte2.YOUT
  N3: Parte1.A2, Parte2.ZOUT
  N4: Parte1.A3, R4.pin_1, R5.Pin_0
  N5: Parte1.D10_PWM/SS, R6.Pin_0
  N6: Parte1.D11_PWM/MOSI, R3.Pin_0
  N7: Parte1.D12/MISO, R2.Pin_0
  N8: Parte1.D13/SCK, R1.Pin_0
  GND: Parte1.GND, LCD1.V0, LED1.anode, LED3.anode, LED4.anode, LED5.anode, Parte2.GND, R5.Pin_1, RE1.EncoderPinC
  N9: Parte1.D2, LCD1.RS
  N10: Parte1.D4, RE1.EncoderPinA
  N11: Parte1.D5_PWM, RE1.EncoderPinB
  3V3: Parte1.3V3, Parte2.VCC
  5V: Parte1.5V, LCD1.VSS, R4.pin_0
  N12: LED1.cathode, R6.Pin_1
  N13: LED3.cathode, R3.Pin_1
  N14: LED4.cathode, R2.Pin_1
  N15: LED5.cathode, R1.Pin_1
