# Fritzing sketch wiring_backpackSensor (saved by Fritzing 0.9.1b)
breadboards: 2

parts:
  DFRobot_Bluetooth_V1 = TEL0026-BluetoothV3
  IC1 = IC, DIP package, 16 pins [chip_label=L293D]
  Parte3 = Arduino Uno (Rev3)
  R9 = Resistor [tolerance=±10% resistance=10k package=THT]
  R10 = Photocell (LDR) [package=THT]
  LED6 = LED - 5mm [color="Yellow (595nm)" package="5 mm [THT]"]
  LED7 = LED - 5mm [color="Red (633nm)" package="5 mm [THT]"]
  LED8 = LED - 5mm [color="Green (560nm)" package="5 mm [THT]"]
  R11 = Resistor [tolerance=±5% resistance=270 package=THT]
  R12 = Resistor [tolerance=±5% resistance=10k package=THT]
  R13 = Resistor [tolerance=±5% resistance=270 package=THT]
  R14 = Resistor [tolerance=±5% resistance=270 package=THT]
  Parte4 = Triple Axis Accelerometer Breakout - ADXL335
  R15 = Temperature Sensor (Thermistor) [thermistor_type=NTC package=THT]

nets:
  N1: DFRobot_Bluetooth_V1.TXD, Parte3.D2
  N2: DFRobot_Bluetooth_V1.VCC, IC1.pin3
  GND: DFRobot_Bluetooth_V1.GND#connector1pad-4-5-0-3-1-0, IC1.pin4, Parte3.GND, R10.pin_0, LED6.anode, LED7.anode, LED8.anode, R12.Pin_1, Parte4.GND
  N3: DFRobot_Bluetooth_V1.RXD, Parte3.D3_PWM
  N4: IC1.pin1, Parte3.D8
  N5: IC1.pin2, IC1.pin8, IC1.pin16, Parte3.5V, R9.Pin_1, R15.pin_0
  N6: Parte3.A0, Parte4.XOUT
  N7: Parte3.A1, Parte4.YOUT
  N8: Parte3.A2, Parte4.ZOUT
  N9: Parte3.A3, R12.Pin_0, R15.pin_1
  N10: Parte3.A4/SDA, R9.Pin_0, R10.pin_1
  N11: Parte3.D10_PWM/SS, R11.Pin_0
  N12: Parte3.D11_PWM/MOSI, R13.Pin_0
  N13: Parte3.D12/MISO, R14.Pin_0
  3V3: Parte3.3V3, Parte4.VCC
  N14: LED6.cathode, R14.Pin_1
  N15: LED7.cathode, R13.Pin_1
  N16: LED8.cathode, R11.Pin_1
